# Fritzing sketch diagram_pas_throttle (saved by Fritzing 0.9.10b)
circuit board: 8.46667cm x 5.64444cm
perfboards: 1

parts:
  R1 = Resistor [tolerance=±1% power=0.25 resistance=1k package=THT]
  J4 = female pin header, 3 pins [form="♀ (female)"]
  Composant1 = Arduino Nano (Rev3.0)
  C1 = Electrolytic Capacitor [capacitance=0.1µF voltage=35V package="100 mil [THT, electrolytic]"]
  J5 = female pin header, 2 pins [form="♀ (female)"]
  J6 = female alternating pin header, 3 pins [form="♀ (female)"]
  J3 = female pin header, 2 pins [form="♀ (female)"]

nets:
  N1: R1.Pin_0, Composant1.D10
  N2: R1.Pin_1, C1.+, J3.pin1
  N3: J4.pin1, Composant1.D2
  GND: J4.pin2, Composant1.GND, C1.-, J5.pin2, J6.pin2, J3.pin2
  5V: J4.pin3, Composant1.5V, J6.pin1
  N4: Composant1.VIN, J5.pin1
  N5: Composant1.A0, J6.pin3

notes:
  + Vin (7V-12V)
  Common GND
  +5V arduino
  Signal (PWM D10)
  Gnd
  Signal (D2)
  e-bike PAS
  LED BUILTIN (D13)
  +
  +5V
  S
  RC filter
  not mandatory, to be tested
  (with controler)
  PAS to throttle, Chris74
  A0
  Throttle (if needed)
  not mandatory
  Vin 7-12V
  Gnd commun
  Controler (throttle in)
